# Fritzing sketch vmeter (saved by Fritzing 0.9.3b)
breadboards: 1

parts:
  Trinket_M0 = Adafruit Trinket M0 [part_number="Adafruit #3500"]
  Bauteil1 = Adafruit DS3231 [part_number="Adafruit #3013"]
  S1 = Pushbutton [package="[THT]"]
  R1 = Resistor [tolerance=±5% resistance=10k package=THT]
  R2 = Resistor [tolerance=±5% resistance=15k package=THT]
  S2 = Toggle Switch [package=THT]
  R3 = Resistor [tolerance=±5% resistance=2.2k package=THT]
  R4 = Resistor [tolerance=±5% resistance=2.2k package=THT]

nets:
  GND: Trinket_M0.GND, Bauteil1.GND, R2.Pin_0, S2.L1
  N1: Trinket_M0.D4_A2_PA06_TXD_MOSI, S2.COM
  N2: Trinket_M0.D3_A3_PA07_RXD_SCK, S1.Pin_3, S1.Pin_4
  3.3V: Trinket_M0.3.3V, Bauteil1.Vin, S1.Pin_1, S1.Pin_2, R3.Pin_0, R4.Pin_0
  N3: Trinket_M0.D2_A1_PA09_SCL_MISO, Bauteil1.SCL, R4.Pin_1
  N4: Trinket_M0.D1_A0_PA02, R1.Pin_1, R2.Pin_1
  N5: Trinket_M0.D0_A4_PA08_SDA, Bauteil1.SDA, R3.Pin_1
  Uin: R1.Pin_0

custom parts:
  Adafruit DS3231: The datasheet for the DS3231 explains that this part is an "Extremely Accurate I²C-Integrated RTC/TCXO/Crystal". And, hey, it does exactly what it says on the tin! This Real Time Clock (RTC) is the most precise you can get in a small, low power package. Most RTCs use an external 32kHz timing crystal that is used to keep time with low current draw. And that's all well and good, but those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
